# Fritzing sketch buttons (saved by Fritzing 0.9.3b)
breadboards: 1

parts:
  Part1 = Arduino Uno (Rev3)
  LED1 = LED - 5mm [color="Red (633nm)" package="5 mm [THT]"]
  R1 = Resistor [tolerance=±5% resistance=220 package=THT]
  S1 = Pushbutton [package="[THT]"]
  S2 = Pushbutton [package="[THT]"]

nets:
  N1: Part1.D8, S2.Pin_3, S2.Pin_4
  N2: Part1.D9_PWM, Part1.D5_PWM, R1.Pin_1, S1.Pin_3, S1.Pin_4
  N3: Part1.GND, LED1.cathode, S1.Pin_1, S1.Pin_2, S2.Pin_1, S2.Pin_2
  N4: LED1.anode, R1.Pin_0
